// Logisim project mult4.circ as structural Verilog: 1 circuit, main circuit main
module main (
  input  A3,
  input  A2,
  input  A1,
  input  A0,
  input  B3,
  input  B2,
  input  B1,
  input  B0
);

  wire adder_1_out, adder_2_out, adder_3_out, adder_4_out, adder_5_out, adder_6_out, adder_7_out, and_1_out,
       and_2_out, and_3_out, and_4_out, and_5_out, and_6_out, and_7_out, and_8_out, and_9_out, and_10_out,
       and_11_out, and_12_out, and_13_out, and_14_out, and_15_out, and_16_out;

  and and_1 (and_1_out, A0, A0);
  and and_2 (and_2_out, A0, A0);
  and and_3 (and_3_out, A0, A0);
  and and_4 (and_4_out, A0, A0);
  and and_5 (and_5_out, A0, A0);
  and and_6 (and_6_out, A0, A0);
  and and_7 (and_7_out, A0, A0);
  and and_8 (and_8_out, A0, A0);
  and and_9 (and_9_out, A0, A0);
  and and_10 (and_10_out, A0, A0);
  and and_11 (and_11_out, A0, A0);
  and and_12 (and_12_out, A0, A0);
  and and_13 (and_13_out, A0, A0);
  and and_14 (and_14_out, A0, A0);
  and and_15 (and_15_out, A0, A0);
  and and_16 (and_16_out, A0, A0);
  Adder #(.width(1)) adder_1 (.a(and_2_out), .b(and_3_out), .out(adder_1_out));  // open: cin, cout
  Adder #(.width(1)) adder_2 (.a(and_4_out), .b(and_5_out), .out(adder_2_out));  // open: cin, cout
  Adder #(.width(1)) adder_3 (.a(and_7_out), .b(and_8_out), .out(adder_3_out));  // open: cin, cout
  Adder #(.width(1)) adder_4 (.a(and_9_out), .b(and_10_out), .out(adder_4_out));  // open: cin, cout
  Adder #(.width(1)) adder_5 (.a(and_11_out), .b(and_12_out), .out(adder_5_out));  // open: cin, cout
  Adder #(.width(1)) adder_6 (.a(and_14_out), .b(and_15_out), .out(adder_6_out));  // open: cin, cout
  Adder #(.width(1)) adder_7 (.a(adder_2_out), .b(and_6_out), .out(adder_7_out));  // open: cin, cout
  Adder #(.width(1)) adder_8 (.a(adder_3_out), .b(adder_4_out), .out(adder_7_out));  // open: cin, cout
  Adder #(.width(1)) adder_9 (.a(adder_5_out), .b(and_13_out), .out(adder_7_out));  // open: cin, cout
  _7_Segment_Display u_7_segment_display_1 (
    .g(and_16_out), .f(adder_6_out), .a(and_1_out), .b(adder_1_out), .e(adder_7_out), .d(adder_7_out),
    .c(adder_7_out));  // open: dp

  assign A1 = A0;
  assign A2 = A0;
  assign A3 = A0;
  assign B0 = A0;
  assign B1 = A0;
  assign B2 = A0;
  assign B3 = A0;
endmodule
