// Logisim project somadorCLA.circ as structural Verilog: 1 circuit, main circuit main
module main (
  input  A4,
  input  A3,
  input  B4,
  input  B3,
  input  A2,
  input  A1,
  input  B2,
  input  B1
);

  wire n7447_1_pin1, n7447_1_pin2, n7447_1_pin6, n7447_1_pin7, n7447_1_pin9, n7447_1_pin10, n7447_1_pin11,
       n7447_1_pin12, n7447_1_pin13, n7447_1_pin14, n7447_1_pin15, n7447_2_pin9, n7447_2_pin10,
       n7447_2_pin11, n7447_2_pin12, n7447_2_pin13, n7447_2_pin14, n7447_2_pin15, n7447_3_pin9,
       n7447_3_pin10, n7447_3_pin11, n7447_3_pin12, n7447_3_pin13, n7447_3_pin14, n7447_3_pin15;

  _7447 #(.ShowInternalStructure("true")) u_7447_1 (
    .pin1(n7447_1_pin1), .pin2(n7447_1_pin2), .pin6(n7447_1_pin6), .pin7(n7447_1_pin7),
    .pin15(n7447_1_pin15), .pin14(n7447_1_pin14), .pin13(n7447_1_pin13), .pin12(n7447_1_pin12),
    .pin11(n7447_1_pin11), .pin10(n7447_1_pin10), .pin9(n7447_1_pin9));  // open: pin3, pin4, pin5
  _74283 #(.ShowInternalStructure("true")) u_74283_1 (
    .pin1(n7447_1_pin1), .pin2(B2), .pin3(A2), .pin4(n7447_1_pin7), .pin5(A1), .pin6(B1), .pin15(B3),
    .pin14(A3), .pin13(n7447_1_pin2), .pin12(A4), .pin11(B4), .pin10(n7447_1_pin6));  // open: pin7, pin9
  _7_Segment_Display #(.active("false")) soma (
    .g(n7447_1_pin14), .f(n7447_1_pin15), .a(n7447_1_pin13), .b(n7447_1_pin12), .e(n7447_1_pin9),
    .d(n7447_1_pin10), .c(n7447_1_pin11));  // open: dp
  _7447 #(.ShowInternalStructure("true")) u_7447_2 (
    .pin1(B2), .pin2(B3), .pin6(B4), .pin7(B1), .pin15(n7447_2_pin15), .pin14(n7447_2_pin14),
    .pin13(n7447_2_pin13), .pin12(n7447_2_pin12), .pin11(n7447_2_pin11), .pin10(n7447_2_pin10),
    .pin9(n7447_2_pin9));  // open: pin3, pin4, pin5
  _7_Segment_Display #(.active("false")) u_7_segment_display_1 (
    .g(n7447_2_pin14), .f(n7447_2_pin15), .a(n7447_2_pin13), .b(n7447_2_pin12), .e(n7447_2_pin9),
    .d(n7447_2_pin10), .c(n7447_2_pin11));  // open: dp
  _7447 #(.ShowInternalStructure("true")) u_7447_3 (
    .pin1(A2), .pin2(A3), .pin6(A4), .pin7(A1), .pin15(n7447_3_pin15), .pin14(n7447_3_pin14),
    .pin13(n7447_3_pin13), .pin12(n7447_3_pin12), .pin11(n7447_3_pin11), .pin10(n7447_3_pin10),
    .pin9(n7447_3_pin9));  // open: pin3, pin4, pin5
  _7_Segment_Display #(.active("false")) u_7_segment_display_2 (
    .g(n7447_3_pin14), .f(n7447_3_pin15), .a(n7447_3_pin13), .b(n7447_3_pin12), .e(n7447_3_pin9),
    .d(n7447_3_pin10), .c(n7447_3_pin11));  // open: dp

  // Notes on the sheet:
  //   SOMA
  //   B
  //   A
endmodule
